# Fritzing sketch wiring-diagram (saved by Fritzing 0.8.3b)

parts:
  RaspberryPi1 = Raspberry Pi Model B
  J1 = Piezo Speaker

nets:
  N1: RaspberryPi1.GND, J1.pin1
  N2: RaspberryPi1.#22, J1.pin2

custom parts:
  Raspberry Pi Model B: Raspberry Pi (Model B)
